# Fritzing sketch Combo Lock (saved by Fritzing 0.9.4)
breadboards: 1

parts:
  SW1 = DIP Switch 8 Position [package=dipswitch-08]
  Part1 = Arduino Uno (Rev3)
  S1 = Pushbutton [package="[THT]"]
  R1 = Resistor [tolerance=±5% resistance=220 package=THT]
  R2 = Resistor [tolerance=±5% resistance=220 package=THT]
  R3 = Resistor [tolerance=±5% resistance=220 package=THT]
  R4 = Resistor [tolerance=±5% resistance=220 package=THT]
  LED1 = LED - 3mm [color="Red (633nm)" package="3 mm [THT]"]
  LED2 = LED - 3mm [color="Red (633nm)" package="3 mm [THT]"]
  LED3 = LED - 3mm [color="Red (633nm)" package="3 mm [THT]"]
  R5 = Resistor [tolerance=±5% resistance=220 package=THT]
  R6 = Resistor [tolerance=±5% resistance=220 package=THT]
  R7 = Resistor [tolerance=±5% resistance=220 package=THT]
  R8 = Resistor [tolerance=±5% resistance=220 package=THT]
  R9 = Resistor [tolerance=±5% resistance=220 package=THT]
  R10 = Resistor [tolerance=±5% resistance=220 package=THT]
  R11 = Resistor [tolerance=±5% resistance=220 package=THT]
  R12 = Resistor [tolerance=±5% resistance=220 package=THT]

nets:
  N1: SW1.1, SW1.2, SW1.3, SW1.4, SW1.5, SW1.6, SW1.7, SW1.8, Part1.D13/SCK, Part1.VIN, S1.Pin_3, S1.Pin_4, R1.Pin_0
  N2: SW1.9, Part1.D12/MISO, R8.Pin_0
  N3: SW1.10, Part1.D11_PWM/MOSI, R7.Pin_0
  N4: SW1.11, Part1.D10_PWM/SS, R6.Pin_0
  N5: SW1.12, Part1.D9_PWM, R5.Pin_0
  N6: SW1.13, Part1.D8, R9.Pin_1
  N7: SW1.14, Part1.D7, R10.Pin_1
  N8: SW1.15, Part1.D6_PWM, R11.Pin_1
  N9: SW1.16, Part1.D5_PWM, R12.Pin_1
  N10: Part1.D2, R4.Pin_1
  N11: Part1.D3_PWM, R3.Pin_1
  N12: Part1.D4, R2.Pin_1
  N13: Part1.GND, R1.Pin_1, LED1.cathode, LED2.cathode, LED3.cathode, R5.Pin_1, R6.Pin_1, R7.Pin_1, R8.Pin_1, R9.Pin_0, R10.Pin_0, R11.Pin_0, R12.Pin_0
  N14: S1.Pin_1, S1.Pin_2
  N15: R2.Pin_0, LED3.anode
  N16: R3.Pin_0, LED2.anode
  N17: R4.Pin_0, LED1.anode
